# Fritzing sketch 231118_Pflanzensensor_geroutet (saved by Fritzing 1.0.1rc)
circuit board: 6.6cm x 6.6cm
breadboards: 1

parts:
  Capacitive_Soil_Moisture_Sensor2 = DFRobot Capacitive Soil Moisture Sensor V1.0 [part_number=SEN0193]  # not connected
  IC3 = IC, DIP package, 16 pins [chip_label="IC 4051"]
  R2 = Resistor [tolerance=±5% resistance=33 power=0.25W package="0805 [SMD]"]
  LED_rot = smd LED [color="Red (633nm)" current=30mA package="0805 [SMD]"]
  LED_grün = smd LED [color="Green (560nm)" current=30mA package="0805 [SMD]"]
  LED_gelb = smd LED [color="Yellow (585nm)" current=30mA package="0805 [SMD]"]
  Fotowiderstand = Photocell (LDR) [power=0.25W dark_resistance_@0.01lx=300kΩ light_resistance_@100lx=400Ω luminance=10lx package=THT]
  R5 = Resistor [tolerance=±5% resistance=10k power=0.25W package="0805 [SMD]"]
  DHT2 = DHT11 Humitidy and Temperature Sensor
  R6 = Resistor [tolerance=±5% resistance=10k power=0.25W package="0805 [SMD]"]
  JP5_Ext_Strom = Header 2 [package=jst-2-smd]
  Pins_Display = female pin header, 4 pins [form="♀ (female)"]
  X2_X3 = female pin header, 2 pins [form="♀ (female)"]
  SD1_SD2_SD3_D8 = female pin header, 4 pins [form="♀ (female)"]
  JP4_Soil_Stecker = Header 3 [package=jst-3-smd]
  Mod4 = Amica NodeMCU DEVKIT 1.0  # not connected
  Pins_ESP_1 = single row smd female pin header, 15 pins [form="♀ (female)"]
  Pins_ESP_2 = single row smd female pin header, 15 pins [form="♀ (female)"]
  OLED2 = SSD1306 0.96in 128x64 I2C Monochrome OLED Display  # not connected
  Pins_Display1 = female pin header, 4 pins [form="♀ (female)"]

nets:
  N1: IC3.pin3, Pins_ESP_2.pin15
  N2: IC3.pin8, IC3.pin9, IC3.pin10, R2.Pin_0, R5.Pin_1, DHT2.GND, JP5_Ext_Strom.1, Pins_Display.pin4, JP4_Soil_Stecker.1, Pins_ESP_1.pin2, Pins_ESP_1.pin9, Pins_ESP_2.pin2, Pins_Display1.pin1
  N3: IC3.pin11, Pins_ESP_1.pin15
  N4: IC3.pin12, X2_X3.pin2
  N5: IC3.pin13, Fotowiderstand.pin_1, R5.Pin_0
  N6: IC3.pin14, JP4_Soil_Stecker.3
  N7: IC3.pin15, X2_X3.pin1
  N8: IC3.pin16, Fotowiderstand.pin_0, DHT2.VDD, R6.Pin_1, Pins_Display.pin3, JP4_Soil_Stecker.2, Pins_ESP_1.pin10, Pins_Display1.pin2
  N9: R2.Pin_1, LED_rot.cathode, LED_grün.cathode, LED_gelb.cathode
  N10: LED_rot.anode, Pins_ESP_1.pin6
  N11: LED_grün.anode, Pins_ESP_1.pin8
  N12: LED_gelb.anode, Pins_ESP_1.pin7
  N13: DHT2.DATA, R6.Pin_0, Pins_ESP_1.pin11
  N14: JP5_Ext_Strom.2, Pins_ESP_2.pin1
  N15: Pins_Display.pin1, Pins_ESP_1.pin13, Pins_Display1.pin4
  N16: Pins_Display.pin2, Pins_ESP_1.pin14, Pins_Display1.pin3
  N17: SD1_SD2_SD3_D8.pin1, Pins_ESP_1.pin5
  N18: SD1_SD2_SD3_D8.pin2, Pins_ESP_2.pin10
  N19: SD1_SD2_SD3_D8.pin3, Pins_ESP_2.pin11
  N20: SD1_SD2_SD3_D8.pin4, Pins_ESP_2.pin12

notes:
  was noch fehlt:
  – extra pins + lötlöcher
  – richtige beschriftung
  – logos
  ggfs noch ändern:
  – photosensor > smd
  – buchsen, steckleisten

custom parts:
  DFRobot Capacitive Soil Moisture Sensor V1.0: DFRobot Capacitive Soil Moisture Sensor V1.0 This product measures soil moisture levels by capacitive sensing, rather than resistive sensing like other types of moisture sensor. It is made of a corrosion resistant material giving it a long service life. Insert it into soil and impress your friends with the real-time soil moisture data! The product includes an on-board voltage regulator which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
  DHT11 Humitidy and Temperature Sensor: DHT11 Humidity and Temperature Sensor
