# Fritzing sketch 231120_Pflanzensensor_geroutet_V2 (saved by Fritzing 1.0.1rc)
circuit board: 6.6cm x 6.6cm
breadboards: 1

parts:
  Analog_Multiplexer = IC, DIP package, 16 pins [chip_label="IC 4051"]
  R = Resistor [tolerance=±5% resistance=33 power=0.25W package="0805 [SMD]"]
  LED_rot = smd LED [color="Red (633nm)" current=30mA package="0805 [SMD]"]
  LED_grün = smd LED [color="Green (560nm)" current=30mA package="0805 [SMD]"]
  LED_gelb = smd LED [color="Yellow (585nm)" current=30mA package="0805 [SMD]"]
  Lichtsensor = Photocell (LDR) [power=0.25W dark_resistance_@0.01lx=300kΩ light_resistance_@100lx=400Ω luminance=10lx package=THT]
  10kΩ = Resistor [tolerance=±5% resistance=10k power=0.25W package="0805 [SMD]"]
  Temp_+_Humidity = DHT11 Humitidy and Temperature Sensor
  10kΩ_2 = Resistor [tolerance=±5% resistance=10k power=0.25W package="0805 [SMD]"]
  X3_X2 = female pin header, 2 pins [form="♀ (female)"]
  SD3_SD2_SD1_D8 = female pin header, 4 pins [form="♀ (female)"]
  Mod4 = Amica NodeMCU DEVKIT 1.0  # not connected
  Soil_Moisture = Header 3 [package=jst-3-pth]
  Ext_Power = Header 2 [package=jst-2-pth-kit]
  J13 = female pin header, 15 pins [form="♀ (female)"]  # not connected
  ESP = Header_ESP_2 - 15 pins [form="♀ (female)" package=THT]
  Display_Pins_2 = Header Display [form="♀ (female)" package=THT]
  Display_Pins_1 = Header Display [form="♀ (female)" package=THT]
  USB = Header_ESP_1 - 15 pins [form="♀ (female)" package=THT]

nets (from the pcb view):
  N1: Analog_Multiplexer.pin3, USB.A0
  GND: Analog_Multiplexer.pin8, Analog_Multiplexer.pin9, Analog_Multiplexer.pin10, R.Pin_0, Temp_+_Humidity.GND, Soil_Moisture.1, Display_Pins_2.GND, Display_Pins_1.GND, USB.GND#5
  N2: Analog_Multiplexer.pin11, ESP.D0
  N3: Analog_Multiplexer.pin12, X3_X2.pin2
  N4: Analog_Multiplexer.pin13, 10kΩ.Pin_1, ESP.GND
  N5: Analog_Multiplexer.pin14, Soil_Moisture.3
  N6: Analog_Multiplexer.pin15, X3_X2.pin1
  3V3: Analog_Multiplexer.pin16, Lichtsensor.pin_0, Temp_+_Humidity.VDD, 10kΩ_2.Pin_1, Soil_Moisture.2, ESP.3V3, Display_Pins_2.VCC, Display_Pins_1.VCC, USB.3V3
  N7: R.Pin_1, LED_rot.cathode, LED_grün.cathode, LED_gelb.cathode
  N8: LED_rot.anode, ESP.D7
  N9: LED_grün.anode, ESP.D5
  N10: LED_gelb.anode, ESP.D6
  N11: Lichtsensor.pin_1, 10kΩ.Pin_0
  N12: Temp_+_Humidity.DATA, 10kΩ_2.Pin_0, ESP.D4
  N13: SD3_SD2_SD1_D8.pin1, ESP.D8
  N14: SD3_SD2_SD1_D8.pin2, USB.SD1
  N15: SD3_SD2_SD1_D8.pin3, USB.SD2
  N16: SD3_SD2_SD1_D8.pin4, USB.SD3
  N17: Ext_Power.1, USB.GND#1
  N18: Ext_Power.2, USB.Vin
  N19: ESP.D1, Display_Pins_2.SCL, Display_Pins_1.SCL
  N20: ESP.D2, Display_Pins_2.SDA, Display_Pins_1.SDA

notes:
  was noch fehlt:
  – extra pins + lötlöcher
  – richtige beschriftung
  – logos
  ggfs noch ändern:
  – photosensor > smd
  – buchsen, steckleisten
  Vin
  GND

custom parts:
  DHT11 Humitidy and Temperature Sensor: DHT11 Humidity and Temperature Sensor
  Header_ESP_2 - 15 pins: Header for ESP 2
  Header_ESP_1 - 15 pins: Header for ESP 1
