# Fritzing sketch 240301_Pflanzensensor_geroutet_V9 (saved by Fritzing 1.0.1rc)
circuit board: 6.97314cm x 21.6237cm
breadboards: 1

parts:
  Analog_Multiplexer = IC, DIP package, 16 pins [chip_label="IC 4051"]
  Licht = Photocell (LDR) [power=0.25W dark_resistance_@0.01lx=300kΩ light_resistance_@100lx=400Ω luminance=10lx package=THT]
  Temp_+_Humidity = DHT11 Humitidy and Temperature Sensor
  Vin = Header 2 [part_number=S2B-PH-K-S package=jst-2-pth-kit]
  J13 = female pin header, 15 pins [form="♀ (female)"]  # not connected
  Display_1 = Header Display [form="♀ (female)" package=THT]
  USB = Header_ESP_1 - 15 pins [form="♀ (female)" package=THT]
  G = LED - 3mm [color="Green (560nm)" current=30mA package="3 mm [THT]"]
  LED_gelb = LED - 3mm [color="Yellow (585nm)" current=30mA package="3 mm [THT]"]
  R2_(LEDs) = Resistor [tolerance=±5% power=0.25W resistance=33 package=THT]
  R3_(DHT) = Resistor [tolerance=±5% power=0.25W resistance=10k package=THT]
  Lötloch_+ = Header 1 [package=1x01_offset]
  Lötloch_- = Header 1 [package=1x01_offset]
  ESP3 = Header_ESP_2 - 15 pins [form="♀ (female)" package=THT]
  Mod4 = Amica NodeMCU DEVKIT 1.0  # not connected
  SD3_SD2_SD1_D8_1 = female pin header, 3 pins [form="♀ (female)"]
  SD3_SD2_SD1_D8_2 = female pin header, 3 pins [form="♀ (female)"]
  SD3_SD2_SD1_D8_3 = female pin header, 3 pins [form="♀ (female)"]
  Lötloch_+1 = Header 1 [package=1x01_offset]
  Lötloch_+2 = Header 1 [package=1x01_offset]
  ESP = Header_ESP_2 - 15 pins [form="♀ (female)" package=THT]
  J14 = single row smd female pin header, 15 pins [form="♀ (female)"]  # not connected
  J15 = single row smd female pin header, 15 pins [form="♀ (female)"]  # not connected
  root1 = male pin header, 3 pins [form="♂ (male)"]
  root2 = male pin header, 3 pins [form="♂ (male)"]
  Pad2 = Pad [width=10 height=10 connect=center]  # not connected
  root3 = male pin header, 3 pins [form="♂ (male)"]
  root4 = male pin header, 3 pins [form="♂ (male)"]
  root5 = male pin header, 3 pins [form="♂ (male)"]
  root6 = male pin header, 3 pins [form="♂ (male)"]
  R1_(Photocell) = Resistor [tolerance=±5% power=0.25W resistance=10k package=THT]
  LED_rot = LED - 3mm [color="Red (633nm)" current=30mA package="3 mm [THT]"]  # not connected

nets:
  N1: Analog_Multiplexer.pin1, root2.pin1
  N2: Analog_Multiplexer.pin3, USB.A0
  N3: Analog_Multiplexer.pin4, Licht.pin_1, R1_(Photocell).Pin_0
  N4: Analog_Multiplexer.pin5, root3.pin1
  GND: Analog_Multiplexer.pin7, Analog_Multiplexer.pin8, Temp_+_Humidity.GND, Vin.2, Display_1.GND, USB.GND, R2_(LEDs).Pin_0, Lötloch_-.1, ESP3.GND, SD3_SD2_SD1_D8_1.pin2, SD3_SD2_SD1_D8_2.pin2, SD3_SD2_SD1_D8_3.pin2, Lötloch_+2.1, ESP.GND, root1.pin3, root2.pin3, root3.pin3, root4.pin1, root5.pin1, root6.pin1, R1_(Photocell).Pin_1
  N5: Analog_Multiplexer.pin9, ESP3.D0, ESP.D0
  N6: Analog_Multiplexer.pin10, ESP3.D4, ESP.D4
  N7: Analog_Multiplexer.pin11, ESP3.D8, ESP.D8
  N8: Analog_Multiplexer.pin12, root5.pin3
  N9: Analog_Multiplexer.pin13, root4.pin3
  N10: Analog_Multiplexer.pin14, root6.pin3
  N11: Analog_Multiplexer.pin15, root1.pin1
  3V3: Analog_Multiplexer.pin16, Licht.pin_0, Temp_+_Humidity.VDD, Display_1.VCC, USB.3V3, R3_(DHT).Pin_1, Lötloch_+.1, ESP3.3V3, SD3_SD2_SD1_D8_1.pin3, SD3_SD2_SD1_D8_2.pin3, SD3_SD2_SD1_D8_3.pin3, ESP.3V3, root1.pin2, root2.pin2, root3.pin2, root4.pin2, root5.pin2, root6.pin2
  N12: Temp_+_Humidity.DATA, R3_(DHT).Pin_0
  N13: Vin.1, USB.Vin, Lötloch_+1.1
  N14: Display_1.SDA, ESP3.D2, ESP.D2
  N15: Display_1.SCL, ESP3.D1, ESP.D1
  N16: USB.SD1, SD3_SD2_SD1_D8_3.pin1
  N17: USB.SD2, SD3_SD2_SD1_D8_2.pin1
  N18: USB.SD3, SD3_SD2_SD1_D8_1.pin1
  N19: G.cathode, LED_gelb.cathode, R2_(LEDs).Pin_1
  N20: G.anode, ESP3.D5, ESP.D5
  N21: LED_gelb.anode, ESP3.D6, ESP.D6
  N22: ESP3.D3, ESP.D3
  N23: ESP3.D7, ESP.D7
  N24: ESP3.RX, ESP.RX
  N25: ESP3.TX, ESP.TX

notes:
  Änderungen 23.11.23
  – Extra Pins Display gedreht und Position geändert, damit Lichtsensor in jedem Fall oben ist
  – Position Lichtsensor
  – Korrektur Multiplexer: GND, B auf D3/ESP
  – Platz für DHT22 gemacht
  – Loch zum Fixieren von DHT22
  – Platz für größeren ESP gemacht
  > insgesamt vergrößert (70x70mm)
  Änderungen 14.1.24
  – DHT von D4 auf D3
  – Photosensor von I/O0 auf I/O7
  – B von D3 auf D4
  – A von D0 auf D8
  – C auf D0
  – Pins für + - SD1, + - SD2, + - SD3
  Änderungen 22.1.24
  – Außenstellen Multiplexer
  ?
  Welche Anschlüsse für Multiplexer Pinouts? Wie Bodensensor oder nur Lötlöcher? Oder Buchsen?
  To Dos
  – Logos
  – Form
  ?
  Welche Anschlüsse für Multiplexer Pinouts? Wie Bodensensor oder nur Lötlöcher? Oder Buchsen?
  D0
  D1
  D2
  D3
  D4
  3V3
  GND
  D5
  D6
  D7
  D8
  RX
  TX
  GND
  3V3
  Vin 5V? 7–12V? > 9V Block?
  Welche Stecker?
  JST Connectors
  https://asset.conrad.com/media10/add/160267/c1/-/en/000740232DS01/datenblatt-740232-jst-einbau-stiftleiste-standard-ph-polzahl-gesamt-3-rastermass-2-mm-s3b-ph-k-s-lfsn-1-st.pdf
  Multiplexer Outpins:
  – auf PCB benennen oder nur im Datenblatt?
  – Lötlöcher oder Pins oder eine Mischung?
  SD1–3 Pins ok? Oder lieber Löcher?

custom parts:
  DHT11 Humitidy and Temperature Sensor: DHT11 Humidity and Temperature Sensor
  Header_ESP_1 - 15 pins: Header for ESP 1
  Header_ESP_2 - 15 pins: Header for ESP 2
