# Fritzing sketch 240313_Pflanzensensor_geroutet_V10 (saved by Fritzing 1.0.1rc)
circuit board: 6.94056cm x 20.9434cm
breadboards: 1

parts:
  Analog_Multiplexer = IC, DIP package, 16 pins [chip_label=CD4051BE mpn=CD4051BE]
  Temp_+_Humidity = DHT11 Humitidy and Temperature Sensor [mpn=DHT11]
  Vin = Header 2 [part_number=S2B-PH-K-S mpn=S2B-PH-K-S package=jst-2-pth-kit]
  J13 = female pin header, 15 pins [form="♀ (female)"]  # not connected
  Display_Header = Header Display [form="♀ (female)" mpn=SSW-104-06-T-S-LL package=THT]
  ESP1 = Header_ESP_1 - 15 pins [form="♀ (female)" mpn=A-BL254-EG-Z15D package=THT]
  LED_G = LED - 3mm [color="Green (560nm)" current=20mA mpn=WP3A8GD package="3 mm [THT]"]
  LED_Y = LED - 3mm [color="Yellow (585nm)" current=20mA mpn=WP3A8YD package="3 mm [THT]"]
  ESP3 = Header_ESP_2 - 15 pins [form="♀ (female)" mpn=A-BL254-EG-Z15D package=THT]
  SD3 = female pin header, 3 pins [form="♀ (female)" mpn=SSW-103-06-T-S-LL]
  SD2 = female pin header, 3 pins [form="♀ (female)" mpn=SSW-103-06-T-S-LL]
  SD1 = female pin header, 3 pins [form="♀ (female)" mpn=SSW-103-06-T-S-LL]
  Lötloch_+ = Header 1 [package=1x01_offset]
  Lötloch_- = Header 1 [package=1x01_offset]
  ESP2 = Header_ESP_2 - 15 pins [form="♀ (female)" mpn=A-BL254-EG-Z15D package=THT]
  X2 = male pin header, 3 pins [form="♂ (male)" mpn=68016-403HLF]
  X4 = male pin header, 3 pins [form="♂ (male)" mpn=68016-403HLF]
  X5 = male pin header, 3 pins [form="♂ (male)" mpn=68016-403HLF]
  X0 = male pin header, 3 pins [form="♂ (male)" mpn=68016-403HLF]
  X3 = male pin header, 3 pins [form="♂ (male)" mpn=68016-403HLF]
  X6 = male pin header, 3 pins [form="♂ (male)" mpn=68016-403HLF]
  LED_R = LED - 3mm [color="Red (633nm)" current=20mA mpn=WP3A10ID package="3 mm [THT]"]
  R-G = Resistor [tolerance=±5% resistance=56 power=0.25W mpn=RC0603JR-0756RL package="0603 [SMD]"]
  R-Y = Resistor [tolerance=±5% resistance=62 power=0.25W mpn=RC0603JR-0762RL package="0603 [SMD]"]
  R-R = Resistor [tolerance=±5% resistance=68 power=0.25W mpn=RC0603JR-0768RL package="0603 [SMD]"]
  Photocell = PHOTOCELL [mpn="Adafruit 161" package=photocell]
  R1 = Resistor [tolerance=±5% resistance=10k power=0.25W mpn=RC0603JR-0710KP package="0603 [SMD]"]
  X1 = male pin header, 3 pins [form="♂ (male)" mpn=68016-403HLF]
  R2 = Resistor [tolerance=±5% resistance=10k power=0.25W mpn=RC0603JR-0710KP package="0603 [SMD]"]

nets:
  N1: Analog_Multiplexer.pin1, X4.pin1
  N2: Analog_Multiplexer.pin2, X6.pin3
  N3: Analog_Multiplexer.pin3, ESP1.A0
  N4: Analog_Multiplexer.pin4, Photocell.P$1, R1.Pin_0
  N5: Analog_Multiplexer.pin5, X5.pin1
  GND: Analog_Multiplexer.pin7, Analog_Multiplexer.pin8, Temp_+_Humidity.GND, Vin.2, Display_Header.GND, ESP1.GND, ESP3.GND, SD3.pin2, SD2.pin2, SD1.pin2, Lötloch_-.1, ESP2.GND, X2.pin3, X4.pin3, X5.pin3, X0.pin1, X3.pin1, X6.pin1, R-G.Pin_0, R-Y.Pin_0, R-R.Pin_0, R1.Pin_1, X1.pin1
  N6: Analog_Multiplexer.pin9, ESP3.D0, ESP2.D0
  N7: Analog_Multiplexer.pin10, ESP3.D4, ESP2.D4
  N8: Analog_Multiplexer.pin11, ESP3.D8, ESP2.D8
  N9: Analog_Multiplexer.pin12, X3.pin3
  N10: Analog_Multiplexer.pin13, X0.pin3
  N11: Analog_Multiplexer.pin14, X1.pin3
  N12: Analog_Multiplexer.pin15, X2.pin1
  3V3: Analog_Multiplexer.pin16, Temp_+_Humidity.VDD, Display_Header.VCC, ESP1.3V3, ESP3.3V3, SD3.pin3, SD2.pin3, SD1.pin3, ESP2.3V3, X2.pin2, X4.pin2, X5.pin2, X0.pin2, X3.pin2, X6.pin2, Photocell.P$2, X1.pin2, R2.Pin_1
  N13: Temp_+_Humidity.DATA, ESP3.D3, ESP2.D3, R2.Pin_0
  N14: Vin.1, ESP1.Vin, Lötloch_+.1
  N15: Display_Header.SDA, ESP3.D2, ESP2.D2
  N16: Display_Header.SCL, ESP3.D1, ESP2.D1
  N17: ESP1.SD1, SD1.pin1
  N18: ESP1.SD2, SD2.pin1
  N19: ESP1.SD3, SD3.pin1
  N20: LED_G.cathode, R-G.Pin_1
  N21: LED_G.anode, ESP3.D5, ESP2.D5
  N22: LED_Y.cathode, R-Y.Pin_1
  N23: LED_Y.anode, ESP3.D6, ESP2.D6
  N24: ESP3.D7, ESP2.D7, LED_R.anode
  N25: ESP3.RX, ESP2.RX
  N26: ESP3.TX, ESP2.TX
  N27: LED_R.cathode, R-R.Pin_1

custom parts:
  DHT11 Humitidy and Temperature Sensor: DHT11 Humidity and Temperature Sensor
  Header_ESP_1 - 15 pins: Header for ESP 1
  Header_ESP_2 - 15 pins: Header for ESP 2
