# Fritzing sketch 240521_Pflanzensensor_geroutet_V13.2 (saved by Fritzing 1.0.1rc)
circuit board: 6.94055cm x 20.9434cm
breadboards: 1

parts:
  IC = IC, DIP package, 16 pins [chip_label=CD4051BE mpn=CD4051BE]
  DHT11 = DHT11 Humitidy and Temperature Sensor [mpn=DHT11]
  Vin = Header 2 [part_number=S2B-PH-K-S mpn=S2B-PH-K-S package=jst-2-pth-kit]
  J13 = female pin header, 15 pins [form="♀ (female)"]  # not connected
  DH = Header Display [form="♀ (female)" mpn=SSW-104-06-T-S-LL package=THT]
  ESP1 = Header_ESP_1 - 15 pins [form="♀ (female)" mpn=A-BL254-EG-Z15D package=THT]
  LEDG = LED - 3mm [color="Green (560nm)" current=20mA mpn=WP3A8GD package="3 mm [THT]"]
  LEDY = LED - 3mm [color="Yellow (585nm)" current=20mA mpn=WP3A8YD package="3 mm [THT]"]
  ESP3 = Header_ESP_2 - 15 pins [form="♀ (female)" mpn=A-BL254-EG-Z15D package=THT]
  SD3 = female pin header, 3 pins [form="♀ (female)" mpn=SSW-103-06-T-S-LL]
  SD2 = female pin header, 3 pins [form="♀ (female)" mpn=SSW-103-06-T-S-LL]
  SD1 = female pin header, 3 pins [form="♀ (female)" mpn=SSW-103-06-T-S-LL]
  LL2 = Header 1 [package=1x01_offset]
  LL1 = Header 1 [package=1x01_offset]
  ESP2 = Header_ESP_2 - 15 pins [form="♀ (female)" mpn=A-BL254-EG-Z15D package=THT]
  X2 = male pin header, 3 pins [form="♂ (male)" mpn=68016-403HLF]
  X4 = male pin header, 3 pins [form="♂ (male)" mpn=68016-403HLF]
  X5 = male pin header, 3 pins [form="♂ (male)" mpn=68016-403HLF]
  X0 = male pin header, 3 pins [form="♂ (male)" mpn=68016-403HLF]
  X3 = male pin header, 3 pins [form="♂ (male)" mpn=68016-403HLF]
  X6 = male pin header, 3 pins [form="♂ (male)" mpn=68016-403HLF]
  LEDR = LED - 3mm [color="Red (633nm)" current=20mA mpn=WP3A10ID package="3 mm [THT]"]
  RG = Resistor [tolerance=±5% resistance=56 power=0.25W mpn=RC0603JR-0756RL package="0603 [SMD]"]
  RY = Resistor [tolerance=±5% resistance=62 power=0.25W mpn=RC0603JR-0762RL package="0603 [SMD]"]
  RR = Resistor [tolerance=±5% resistance=68 power=0.25W mpn=RC0603JR-0768RL package="0603 [SMD]"]
  PHR = PHOTOCELL [mpn="Adafruit 161" package=photocell]
  R1 = Resistor [tolerance=±5% resistance=1k power=0.25W mpn=RC0603JR-0710KP package="0603 [SMD]"]
  X1 = male pin header, 3 pins [form="♂ (male)" mpn=68016-403HLF]
  R2 = Resistor [tolerance=±5% resistance=10k power=0.25W mpn=RC0603JR-0710KP package="0603 [SMD]"]
  C2 = Ceramic Capacitor [capacitance=100nF voltage=6.3V package="0805 [SMD, multilayer]"]
  C1 = Electrolytic Capacitor [package="8mm [THT, electrolytic]"]

nets:
  N1: IC.pin1, X4.pin1
  N2: IC.pin2, X6.pin3
  N3: IC.pin3, ESP1.A0
  N4: IC.pin4, PHR.P$1, R1.Pin_0
  N5: IC.pin5, X5.pin1
  GND: IC.pin6, IC.pin7, IC.pin8, DHT11.GND, Vin.2, DH.GND, ESP1.GND, ESP3.GND, SD3.pin2, SD2.pin2, SD1.pin2, LL1.1, ESP2.GND, X2.pin3, X4.pin3, X5.pin3, X0.pin1, X3.pin1, X6.pin1, RG.Pin_0, RY.Pin_0, RR.Pin_0, R1.Pin_1, X1.pin1, C2.1, C1.-
  N6: IC.pin9, ESP3.D0, ESP2.D0
  N7: IC.pin10, ESP3.D4, ESP2.D4
  N8: IC.pin11, ESP3.D8, ESP2.D8
  N9: IC.pin12, X3.pin3
  N10: IC.pin13, X0.pin3
  N11: IC.pin14, X1.pin3
  N12: IC.pin15, X2.pin1
  3V3: IC.pin16, DHT11.VDD, DH.VCC, ESP1.3V3, ESP3.3V3, SD3.pin3, SD2.pin3, SD1.pin3, ESP2.3V3, X2.pin2, X4.pin2, X5.pin2, X0.pin2, X3.pin2, X6.pin2, PHR.P$2, X1.pin2, R2.Pin_1, C2.0
  N13: DHT11.DATA, ESP3.D3, ESP2.D3, R2.Pin_0
  N14: Vin.1, ESP1.Vin, LL2.1, C1.+
  N15: DH.SDA, ESP3.D2, ESP2.D2
  N16: DH.SCL, ESP3.D1, ESP2.D1
  N17: ESP1.SD1, SD1.pin1
  N18: ESP1.SD2, SD2.pin1
  N19: ESP1.SD3, SD3.pin1
  N20: LEDG.cathode, RG.Pin_1
  N21: LEDG.anode, ESP3.D5, ESP2.D5
  N22: LEDY.cathode, RY.Pin_1
  N23: LEDY.anode, ESP3.D6, ESP2.D6
  N24: ESP3.D7, ESP2.D7, LEDR.anode
  N25: ESP3.RX, ESP2.RX
  N26: ESP3.TX, ESP2.TX
  N27: LEDR.cathode, RR.Pin_1

notes:
  geändert 21.5.24
  – INHIBIT auf GND (VEE)
  – Footprint Lichtsensor etwas nach oben verschoben
  – Vorwiderstand Lichtsensor von 10kOhm zu 1kOhm getauscht
  – Beschriftung Analogsensoren verschoben (jetzt darüber)

custom parts:
  DHT11 Humitidy and Temperature Sensor: DHT11 Humidity and Temperature Sensor
  Header_ESP_1 - 15 pins: Header for ESP 1
  Header_ESP_2 - 15 pins: Header for ESP 2
  Electrolytic Capacitor: electrolytic capacitor, 8mm dia
