# Fritzing sketch 231123_Pflanzensensor_geroutet_V4 (saved by Fritzing 1.0.1rc)
circuit board: 7cm x 7cm
breadboards: 1

parts:
  Analog_Multiplexer = IC, DIP package, 16 pins [chip_label="IC 4051"]
  Licht = Photocell (LDR) [power=0.25W dark_resistance_@0.01lx=300kΩ light_resistance_@100lx=400Ω luminance=10lx package=THT]
  Temp_+_Humidity = DHT11 Humitidy and Temperature Sensor
  X3_X2 = female pin header, 2 pins [form="♀ (female)"]
  SD3_SD2_SD1_D8 = female pin header, 4 pins [form="♀ (female)"]
  Mod4 = Amica NodeMCU DEVKIT 1.0  # not connected
  Soil = Header 3 [package=jst-3-pth]
  Vin = Header 2 [package=jst-2-pth-kit]
  J13 = female pin header, 15 pins [form="♀ (female)"]  # not connected
  ESP = Header_ESP_2 - 15 pins [form="♀ (female)" package=THT]
  Display_2 = Header Display [form="♀ (female)" package=THT]
  Display_1 = Header Display [form="♀ (female)" package=THT]
  USB = Header_ESP_1 - 15 pins [form="♀ (female)" package=THT]
  OLED3 = SSD1306 0.96in 128x64 I2C Monochrome OLED Display  # not connected
  G = LED - 3mm [color="Green (560nm)" current=30mA package="3 mm [THT]"]
  LED_gelb = LED - 3mm [color="Yellow (585nm)" current=30mA package="3 mm [THT]"]
  LED_rot = LED - 3mm [color="Red (633nm)" current=30mA package="3 mm [THT]"]
  R = Resistor [tolerance=±5% power=0.25W resistance=33 package=THT]
  10kΩ = Resistor [tolerance=±5% power=0.25W resistance=10k package=THT]
  10kΩ_2 = Resistor [tolerance=±5% power=0.25W resistance=10k package=THT]
  Extrapins_+-_2 = female pin header, 2 pins [form="♀ (female)"]
  Lötloch_+ = Header 1 [package=1x01_offset]
  Lötloch_- = Header 1 [package=1x01_offset]
  Extrapins_+- = female pin header, 2 pins [form="♀ (female)"]
  U2 = NodeMCU V3.0  # not connected
  ESP3 = Header_ESP_2 - 15 pins [form="♀ (female)" package=THT]

nets:
  N1: Analog_Multiplexer.pin3, USB.A0
  GND: Analog_Multiplexer.pin7, Analog_Multiplexer.pin8, Analog_Multiplexer.pin9, Temp_+_Humidity.GND, Soil.1, ESP.GND, Display_2.GND, Display_1.GND, USB.GND#5, R.Pin_0, 10kΩ.Pin_1, Extrapins_+-_2.pin2, Lötloch_-.1, Extrapins_+-.pin1, ESP3.GND
  N2: Analog_Multiplexer.pin10, ESP.D3, ESP3.D3
  N3: Analog_Multiplexer.pin11, ESP.D0, ESP3.D0
  N4: Analog_Multiplexer.pin12, X3_X2.pin2
  N5: Analog_Multiplexer.pin13, Licht.pin_1, 10kΩ.Pin_0
  N6: Analog_Multiplexer.pin14, Soil.3
  N7: Analog_Multiplexer.pin15, X3_X2.pin1
  3V3: Analog_Multiplexer.pin16, Licht.pin_0, Temp_+_Humidity.VDD, Soil.2, ESP.3V3, Display_2.VCC, Display_1.VCC, USB.3V3, 10kΩ_2.Pin_1, Extrapins_+-_2.pin1, Lötloch_+.1, Extrapins_+-.pin2, ESP3.3V3
  N8: Temp_+_Humidity.DATA, ESP.D4, 10kΩ_2.Pin_0, ESP3.D4
  N9: SD3_SD2_SD1_D8.pin1, ESP.D8, ESP3.D8
  N10: SD3_SD2_SD1_D8.pin2, USB.SD1
  N11: SD3_SD2_SD1_D8.pin3, USB.SD2
  N12: SD3_SD2_SD1_D8.pin4, USB.SD3
  N13: Vin.1, USB.GND#1
  N14: Vin.2, USB.Vin
  N15: ESP.D1, Display_2.SCL, Display_1.SCL, ESP3.D1
  N16: ESP.D2, Display_2.SDA, Display_1.SDA, ESP3.D2
  N17: ESP.D5, G.anode, ESP3.D5
  N18: ESP.D6, LED_gelb.anode, ESP3.D6
  N19: ESP.D7, LED_rot.anode, ESP3.D7
  N20: ESP.RX, ESP3.RX
  N21: ESP.TX, ESP3.TX
  N22: G.cathode, LED_gelb.cathode, LED_rot.cathode, R.Pin_1

notes:
  To Do
  – Logos
  – BOM / Bauteile klären
  – Entscheidung Farbe (schwarz?)
  – Passen die Bauteile? Testen z.B. mit etch-copper-top PDF
  – Produzenten vergleichen
  ggfs noch ändern
  – Beschriftung
  – Header
  – Form
  – Anzahl/Position Löcher
  – Bauteilumrisse ausblenden
  Vor der Produktion
  – Kupfer- + Massefüllung
  Vin
  GND
  Änderungen 21.11.23
  – Löcher zum Montieren im Case (es braucht sicher nicht alle, aber so kann man erstmal sehen, wo sie möglich sind)
  – THT LEDs (statt SMD, weil sinnvoller, wenn PCB gecased wird)
  – Position Lichtsensor
  – SMD Widerstände zu THT getauscht (genug Platz, günstiger, übersichtlicheres Routing)
  – Extra Power Out Pins + Lötlöcher eingebaut
  DHT11
  umge-klappt
  VCC
  SCL
  SDA
  - + D
  - +
  +
  -
  USB
  SD3
  SD1
  D8
  SD2
  Photocell
  X2
  G
  X3
  Analog Multiplexer
  Temp + Humidity
  Display 2
  Display 1
  ESP
  Soil Moisture
  Zu klärende (ggfs. zu beschaffende) Bauteile
  – LEDs (klares oder farbiges Gehäuse? eher kleiner Abstrahlwinkel? 3mm oke?)
  – Widerstand LEDs
  – THT Widerstände oke?
  – Vin + Kabel / Batteriecase
  – Header für Bodenfeuchtesensor
  – Schrauben für Display (M2)
  – ggfs. Schraube für DHT22
  DHT22
  umge-klappt (inkl. halbe Pin-Länge)
  Y
  R
  Änderungen 23.11.23
  – Extra Pins Display gedreht und Position geändert, damit Lichtsensor in jedem Fall oben ist
  – Position Lichtsensor
  – Korrektur Multiplexer: GND, B auf D3/ESP
  – Platz für DHT22 gemacht
  – Loch zum Fixieren von DHT22
  – Platz für größeren ESP gemacht
  > insgesamt vergrößert (70x70mm)

custom parts:
  DHT11 Humitidy and Temperature Sensor: DHT11 Humidity and Temperature Sensor
  Header_ESP_2 - 15 pins: Header for ESP 2
  Header_ESP_1 - 15 pins: Header for ESP 1
  NodeMCU V3.0: ESP8266 based NodeMCU
