# Fritzing sketch Pflanzensensor (saved by Fritzing 0.9.10b)
breadboards: 1

parts:
  Mod1 = Amica NodeMCU DEVKIT 1.0
  DHT11_1 = DHT11 module
  Capacitive_Soil_Moisture_Sensor1 = DFRobot Capacitive Soil Moisture Sensor V1.0 [part_number=SEN0193]
  Mod2 = KY-018 Photoresistor Module [package="Breakout board"]
  A1 = BBAA100043
  IC2 = IC, DIP package, 16 pins [chip_label="IC 4051"]
  OLED1 = SSD1306 0.96in 128x64 I2C Monochrome OLED Display
  U1 = NodeMCU V3.0  # not connected

nets:
  VCC: Mod1.pin1, Mod1.pin_10, Mod1.pin_26, DHT11_1.VCC, Capacitive_Soil_Moisture_Sensor1.VCC, Mod2.Vin, IC2.pin16, OLED1.VCC
  GND: Mod1.pin2, Mod1.pin_9, Mod1.pin_25, Mod1.pin_29, DHT11_1.GND, Capacitive_Soil_Moisture_Sensor1.GND, Mod2.-, A1.pin4, IC2.pin7, IC2.pin8, IC2.pin9, OLED1.GND
  N1: Mod1.pin6, A1.pin3
  N2: Mod1.pin7, A1.pin2
  N3: Mod1.pin8, A1.pin1
  N4: Mod1.pin_11, DHT11_1.DATA
  N5: Mod1.pin_12, IC2.pin10
  N6: Mod1.pin_13, OLED1.SDA
  N7: Mod1.pin_14, OLED1.SCL
  N8: Mod1.pin_15, IC2.pin11
  N9: Mod1.pin_16, IC2.pin3
  N10: Capacitive_Soil_Moisture_Sensor1.A, IC2.pin14
  N11: Mod2.S, IC2.pin13

custom parts:
  DHT11 module: https://cdn-learn.adafruit.com/downloads/pdf/dht.pdf DHT11 black pcb module reference by:https://github.com/adafruit/Fritzing-Library/blob/master/parts/DHT11%20Humitidy%20and%20Temperature%20Sensor.fzpz
  DFRobot Capacitive Soil Moisture Sensor V1.0: DFRobot Capacitive Soil Moisture Sensor V1.0 This product measures soil moisture levels by capacitive sensing, rather than resistive sensing like other types of moisture sensor. It is made of a corrosion resistant material giving it a long service life. Insert it into soil and impress your friends with the real-time soil moisture data! The product includes an on-board voltage regulator which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
  KY-018 Photoresistor Module: KY-018 Photoresistor module, used to measure light intensity. It can determine the presence or absence of light.
  BBAA100043: BBAA100043 traffic light module.
  NodeMCU V3.0: ESP8266 based NodeMCU
